// Logisim project main.circ as structural Verilog: 6 circuits, main circuit main_neander
module main_neander (
  input  in_1,
  input  [3:0] in_2,
  input  [3:0] in_3,
  input  in_4
);

  wire and_1_out, CLK, CLK_Op, CLR, clr_RAM, hlt, jump, N, not_1_out, not_2_out, not_3_out, Principal_out, r,
       w, Z;
  wire [3:0] Acc_1, Acc_2, Cnt_1, Cnt_2;
  wire [7:0] dados, ender, MEM_sec, out_dados, ROM;
  wire [11:0] out_rom;

  and and_1 (and_1_out, CLK, not_3_out);
  not not_1 (not_1_out, jump);
  not not_2 (not_2_out, 1'b0);
  LED led_1 (.in(Z));
  LED led_2 (.in(N));
  not not_3 (not_3_out, hlt);
  Counter counter_1 (.load(jump), .D(MEM_sec), .count(not_1_out), .Q(ROM), .clk(and_1_out), .clr(CLR));  // open: carry
  Counter counter_2 (.load(1'b0), .count(not_2_out), .Q({Cnt_1, Cnt_2}), .clk(and_1_out), .clr(CLR));  // open: D, carry
  Hex_Digit_Display hex_digit_display_1 (.value(Acc_2));  // open: dp
  Hex_Digit_Display hex_digit_display_2 (.value(Acc_1));  // open: dp
  ROM #(.dataWidth(12)) rom_1 (.addr(ROM), .data(out_rom), .sel(in_1));
  Multiplexer #(.width(4), .enable("false")) multiplexer_1 (.in0(in_2), .in1(dados[7:4]), .out(Acc_1), .sel(in_4));
  Multiplexer #(.width(4), .enable("false")) multiplexer_2 (.in0(in_3), .in1(dados[3:0]), .out(Acc_2), .sel(in_4));
  Hex_Digit_Display hex_digit_display_3 (.value(Cnt_1));  // open: dp
  Hex_Digit_Display hex_digit_display_4 (.value(Cnt_2));  // open: dp
  Button button_1 (.out(CLR));
  Button button_2 (.out(clr_RAM));
  not not_4 (CLK, Principal_out);
  RAM #(.bus("separate")) ram_1 (
    .addr(ender), .din(dados), .data(out_dados), .str(w), .sel(in_1), .clk(CLK), .ld(r), .clr(clr_RAM));
  Pull_Resistor pull_resistor_1 (.node(out_dados));
  Processador_neander processador_neander_1 (
    .Barramento(out_rom), .\endereço (ender), .in_1(CLK_Op), .in_2(CLR), .escreve(w),
    .in_acc({Acc_1, Acc_2}), .in_load(out_dados), .dados(dados), .Zero(Z), .Neg(N), .Ender_Mem_Sec(MEM_sec),
    .HLT(hlt), .Jump(jump), .le(r));
  Clock #(.highDuration(2), .lowDuration(2)) Principal (.out(Principal_out));
  Clock \Operações  (.out(CLK_Op));

  // Other names for the same wires on the sheet: N_Acc_2[3:0] = dados[3:0]; N_Acc_1[3:0] = dados[7:4]; Ligar = in_1

  // Notes on the sheet:
  //   Ken E. Ccorahua
  //   Acumulador
  //   contents of rom_1 (hex, n*v repeats v):
  //   202 90b 201 303 103 0 204 302 102 0 700 a00
  //   Contador (PC)
endmodule

module Processador_neander (
  input  in_1,
  input  in_2,
  input  [7:0] in_acc,
  input  [7:0] in_load,
  input  [11:0] Barramento,
  output [7:0] dados,
  output escreve,
  output le,
  output [7:0] \endereço ,
  output HLT,
  output [7:0] Ender_Mem_Sec,
  output Jump,
  output Neg,
  output Zero
);

  wire and_1_out, and_2_out, comparator_1_eq, controle_1_lda, controle_1_nop, eh_ula, JMP, JN, JZ, or_1_out,
       or_2_out, or_3_out, or_6_out;
  wire [7:0] acc, controle_barramento_1_out_dados, controlled_buffer_1_out, in_ula, pull_resistor_4_node,
       pull_resistor_5_node, pull_resistor_6_node;

  assign controlled_buffer_1_out = eh_ula ? in_load : 8'bz;  // Controlled_Buffer controlled_buffer_1
  Pull_Resistor pull_resistor_1 (.node(controlled_buffer_1_out));
  Pull_Resistor pull_resistor_2 (.node(Barramento[11:8]));
  Pull_Resistor pull_resistor_3 (.node(in_ula));
  Controle controle_1 (
    .in_1(Barramento[11:8]), .nop(controle_1_nop), .sta(escreve), .lda(controle_1_lda), .jmp(JMP), .jn(JN),
    .jz(JZ), .hlt(HLT), .ula(eh_ula));
  ULA ula_1 (
    .Saida(in_ula), .in_ACC(controlled_buffer_1_out), .Zero(Zero), .anterior(acc),
    .in_controle(Barramento[11:8]), .Negativo(Neg));  // open: Ow
  controle_barramento controle_barramento_1 (
    .in_acc(in_acc), .buff_acc(escreve), .in_load(in_load), .buff_load(controle_1_lda),
    .out_dados(controle_barramento_1_out_dados), .in_ula(in_ula), .buff_ula(eh_ula));
  or or_1 (or_1_out, in_2, controle_1_nop);
  or or_2 (or_2_out, escreve, controle_1_lda, eh_ula);
  or or_3 (or_3_out, JMP, JN, JZ);
  Register Acumulador (.D(in_ula), .en(eh_ula), .Q(acc), .clk(in_1), .clr(or_1_out));
  Register RDM (.D(controle_barramento_1_out_dados), .en(1'b1), .Q(dados), .clk(in_1), .clr(or_1_out));
  Register REM (.D(Barramento[7:0]), .en(or_2_out), .Q(\endereço ), .clk(in_1), .clr(or_1_out));
  Comparator comparator_1 (.a(in_load), .b({8{1'b0}}), .eq(comparator_1_eq));  // open: gt, lt
  and and_1 (and_1_out, comparator_1_eq, JZ);
  and and_2 (and_2_out, in_load[7], JN);
  Pull_Resistor pull_resistor_4 (.node(pull_resistor_4_node));
  Pull_Resistor pull_resistor_5 (.node(pull_resistor_5_node));
  Pull_Resistor pull_resistor_6 (.node(pull_resistor_6_node));
  assign pull_resistor_4_node = JMP ? Barramento[7:0] : 8'bz;  // Controlled_Buffer controlled_buffer_2
  assign pull_resistor_5_node = and_1_out ? Barramento[7:0] : 8'bz;  // Controlled_Buffer controlled_buffer_3
  assign pull_resistor_6_node = and_2_out ? Barramento[7:0] : 8'bz;  // Controlled_Buffer controlled_buffer_4
  or or_4 (le, JZ, controle_1_lda, eh_ula, JN);
  assign Ender_Mem_Sec = pull_resistor_4_node | pull_resistor_5_node | pull_resistor_6_node;  // OR_Gate or_5, 8 bits wide
  or or_6 (or_6_out, JMP, and_1_out, and_2_out);
  and and_3 (Jump, or_3_out, or_6_out);

  // Other names for the same wires on the sheet: inst[3:0] = Barramento[11:8]; clear = in_2; clk = in_1;
  //   in_ar[7:0] = in_load
endmodule

module Controle (
  input  [3:0] in_1,
  output nop,
  output sta,
  output lda,
  output ula,
  output jmp,
  output jn,
  output jz,
  output hlt
);

  wire comparator_4_eq, comparator_4_gt, comparator_5_lt, or_1_out;

  Pull_Resistor pull_resistor_1 (.node(in_1));
  Comparator #(.width(4)) comparator_1 (.a(in_1), .b(4'b0000), .eq(nop));  // open: gt, lt
  Comparator #(.width(4)) comparator_2 (.a(in_1), .b(4'b0001), .eq(sta));  // open: gt, lt
  Comparator #(.width(4)) comparator_3 (.a(in_1), .b(4'b0010), .eq(lda));  // open: gt, lt
  Comparator #(.width(4)) comparator_4 (.a(in_1), .b(4'b0011), .gt(comparator_4_gt), .eq(comparator_4_eq));  // open: lt
  Comparator #(.width(4)) comparator_5 (.a(in_1), .b(4'b0111), .eq(jmp), .lt(comparator_5_lt));  // open: gt
  Comparator #(.width(4)) comparator_6 (.a(in_1), .b(4'b1000), .eq(jn));  // open: gt, lt
  Comparator #(.width(4)) comparator_7 (.a(in_1), .b(4'b1001), .eq(jz));  // open: gt, lt
  Comparator #(.width(4)) comparator_8 (.a(in_1), .b(4'b1010), .eq(hlt));  // open: gt, lt
  or or_1 (or_1_out, comparator_4_gt, comparator_4_eq);
  and and_1 (ula, or_1_out, comparator_5_lt);

  // Notes on the sheet:
  //   NoP
  //   STA
  //   LDA
  //   ULA
  //   JMP
  //   JN
  //   JZ
  //   HLT
endmodule

module ULA (
  input  [3:0] in_controle,
  input  [7:0] anterior,
  input  [7:0] in_ACC,
  output [7:0] Saida,
  output Negativo,
  output Ow,
  output Zero
);

  wire and_1_out, comparator_1_eq, comparator_1_gt, comparator_2_eq, comparator_2_lt, or_1_out, or_2_out;
  wire [6:0] adder_1_out;
  wire [7:0] and_2_out, not_1_out, or_3_out;

  Comparator #(.width(4)) comparator_1 (
    .a(in_controle), .b(4'b0011), .gt(comparator_1_gt), .eq(comparator_1_eq));  // open: lt
  Comparator #(.width(4)) comparator_2 (
    .a(in_controle), .b(4'b0110), .eq(comparator_2_eq), .lt(comparator_2_lt));  // open: gt
  nor nor_1 (Zero, Saida[0], Saida[1], Saida[2], Saida[3], Saida[4], Saida[5], Saida[6], Saida[7]);
  or or_1 (or_1_out, comparator_1_gt, comparator_1_eq);
  or or_2 (or_2_out, comparator_2_eq, comparator_2_lt);
  and and_1 (and_1_out, or_1_out, or_2_out);
  Adder adder_1 (.a(anterior), .b(in_ACC), .out({Negativo, adder_1_out}), .cout(Ow));  // open: cin
  assign not_1_out = ~in_ACC;  // NOT_Gate not_1, 8 bits wide
  assign and_2_out = anterior & in_ACC;  // AND_Gate and_2, 8 bits wide
  assign or_3_out = anterior | in_ACC;  // OR_Gate or_3, 8 bits wide
  Multiplexer #(.select(4), .width(8), .disabled(0)) multiplexer_1 (
    .in3({Negativo, adder_1_out}), .in4(and_2_out), .in5(or_3_out), .in6(not_1_out), .out(Saida),
    .sel(in_controle), .en(and_1_out));  // open: in0, in1, in2, in7, in8, in9, in10, in11, in12, in13, in14, in15

  // Other names for the same wires on the sheet: S[7:0] = Saida
endmodule

module controle_barramento (
  input  [7:0] in_acc,
  input  buff_acc,
  input  [7:0] in_load,
  input  buff_load,
  input  [7:0] in_ula,
  input  buff_ula,
  output [7:0] out_dados
);

  wire [7:0] controlled_buffer_1_out, controlled_buffer_2_out, pull_resistor_2_node;

  assign controlled_buffer_1_out = buff_acc ? in_acc : 8'bz;  // Controlled_Buffer controlled_buffer_1
  assign controlled_buffer_2_out = buff_load ? in_load : 8'bz;  // Controlled_Buffer controlled_buffer_2
  Pull_Resistor pull_resistor_1 (.node(controlled_buffer_2_out));
  Pull_Resistor pull_resistor_2 (.node(pull_resistor_2_node));
  assign pull_resistor_2_node = buff_ula ? in_ula : 8'bz;  // Controlled_Buffer controlled_buffer_3
  Pull_Resistor pull_resistor_3 (.node(controlled_buffer_1_out));
  assign out_dados = controlled_buffer_1_out | controlled_buffer_2_out | pull_resistor_2_node;  // OR_Gate or_1, 8 bits wide
endmodule

module x (
);

  RAM #(.dataWidth(12)) ram_1 ();  // open: addr, data, sel, clk, ld, clr
endmodule
